# Fritzing sketch LED array (cortana-lights and devops-status) (saved by Fritzing 0.9.3b)
breadboards: 1

parts:
  Part1 = Adafruit T-Cobbler Plus [part_number="Adafruit #1989 and #2028"]
  Resistor1 = Resistor [tolerance=±5% resistance=220 package=THT]
  Resistor2 = Resistor [tolerance=±5% resistance=220 package=THT]
  Resistor3 = Resistor [tolerance=±5% resistance=220 package=THT]
  LED1 = LED - 5mm [color="Green (555nm)" package="5 mm [THT]"]
  LED2 = LED - 5mm [color="Yellow (585nm)" package="5 mm [THT]"]
  LED3 = LED - 5mm [color="Red (633nm)" package="5 mm [THT]"]

nets:
  N1: Part1.+3.3V, Resistor1.Pin_1, Resistor2.Pin_1, Resistor3.Pin_1
  N2: Part1.GPIO16, LED3.cathode
  N3: Part1.GPIO20, LED2.cathode
  N4: Part1.GPIO21, LED1.cathode
  N5: Resistor1.Pin_0, LED3.anode
  N6: Resistor2.Pin_0, LED2.anode
  N7: Resistor3.Pin_0, LED1.anode

custom parts:
  Adafruit T-Cobbler Plus: The Raspberry Pi has landed on the Maker World like a 40-GPIO pinned, quad-USB ported, credit card sized bomb of DIY joy. And while you can use most of our great Model B accessories by hooking up our downgrade cable, its probably a good time to upgrade your set up and accessorize using all of the 40 pins. That's why we now carry the Assembled Adafruit Pi T-Cobbler Plus - Breakout + Cable for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
