# Fritzing sketch hello-world-motor (saved by Fritzing 0.9.3b)
breadboards: 1

parts:
  U1 = 2-Channel 5v Relay Shield [package=relay-2ch5v10a]
  Part1 = Adafruit T-Cobbler Plus [part_number="Adafruit #1989 and #2028"]
  VCC1 = Battery
  M1 = DC Motor

nets:
  VCC: U1.VCC, Part1.+5V
  GND: U1.GND, Part1.GND
  N1: U1.IN1, Part1.GPIO17
  N2: U1.K1-In, M1.pin_1
  N3: U1.K1-On, VCC1.+
  N4: VCC1.-, M1.pin_2

custom parts:
  2-Channel 5v Relay Shield: 2 Channel 5v Relay Shield w. 2x SPD-06VDC-SD-C
  Adafruit T-Cobbler Plus: The Raspberry Pi has landed on the Maker World like a 40-GPIO pinned, quad-USB ported, credit card sized bomb of DIY joy. And while you can use most of our great Model B accessories by hooking up our downgrade cable, its probably a good time to upgrade your set up and accessorize using all of the 40 pins. That's why we now carry the Assembled Adafruit Pi T-Cobbler Plus - Breakout + Cable for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
