# Fritzing sketch hello-world-reference (saved by Fritzing 0.9.3b)
breadboards: 1

parts:
  Resistor = Resistor [tolerance=±5% resistance=220 package=THT]
  LED = LED - 5mm [color="Blue (470nm)" package="5 mm [THT]"]
  Part1 = Adafruit T-Cobbler Plus [part_number="Adafruit #1989 and #2028"]

nets:
  N1: Resistor.Pin_0, LED.anode
  N2: Resistor.Pin_1, Part1.GPIO17
  N3: LED.cathode, Part1.GND

custom parts:
  Adafruit T-Cobbler Plus: The Raspberry Pi has landed on the Maker World like a 40-GPIO pinned, quad-USB ported, credit card sized bomb of DIY joy. And while you can use most of our great Model B accessories by hooking up our downgrade cable, its probably a good time to upgrade your set up and accessorize using all of the 40 pins. That's why we now carry the Assembled Adafruit Pi T-Cobbler Plus - Breakout + Cable for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
