# Fritzing sketch motor (saved by Fritzing 0.9.3b)
breadboards: 1

parts:
  Part1 = Adafruit T-Cobbler Plus [part_number="Adafruit #1989 and #2028"]
  U3 = 2-Channel 5v Relay Shield [package=relay-2ch5v10a]
  U4 = 2-Channel 5v Relay Shield [package=relay-2ch5v10a]
  VCC2 = Battery
  M2 = DC Motor

nets:
  GND: Part1.GND, U3.GND, U4.GND
  N1: Part1.GPIO19, U3.IN1
  N2: Part1.GPIO26, U3.IN2
  VCC: Part1.+5V, U3.VCC, U4.VCC
  N3: Part1.GPIO20, U4.IN1
  N4: Part1.GPIO21, U4.IN2
  N5: U3.K1-In, M2.pin_1
  N6: U3.K1-Off, U3.K2-On, U4.K1-On
  N7: U3.K1-On, U3.K2-Off, VCC2.+
  N8: U3.K2-In, M2.pin_2
  N9: U4.K1-In, VCC2.-

custom parts:
  Adafruit T-Cobbler Plus: The Raspberry Pi has landed on the Maker World like a 40-GPIO pinned, quad-USB ported, credit card sized bomb of DIY joy. And while you can use most of our great Model B accessories by hooking up our downgrade cable, its probably a good time to upgrade your set up and accessorize using all of the 40 pins. That's why we now carry the Assembled Adafruit Pi T-Cobbler Plus - Breakout + Cable for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
  2-Channel 5v Relay Shield: 2 Channel 5v Relay Shield w. 2x SPD-06VDC-SD-C
